// Logisim project CPSC359A1.circ as structural Verilog: 2 circuits, main circuit main
module main (
  input  A,
  input  B,
  input  C,
  input  D,
  output a_2,
  output b_2,
  output c_2,
  output d_2,
  output e,
  output f,
  output g
);

  wire and_1_out, and_2_out, and_3_out, and_4_out, and_5_out, and_6_out, and_7_out, and_8_out, and_9_out,
       and_10_out, and_11_out, and_12_out, and_13_out, and_14_out, and_15_out, and_16_out, and_17_out,
       and_18_out, and_19_out, nand_1_out, nand_2_out, nand_3_out, nand_4_out, nand_5_out, nand_6_out,
       nand_7_out, not_1_out, not_2_out, not_3_out, not_4_out, or_1_out, or_2_out, or_3_out, or_4_out,
       or_5_out, or_6_out, or_7_out, or_8_out;

  not not_1 (not_1_out, A);
  not not_2 (not_2_out, B);
  not not_3 (not_3_out, C);
  not not_4 (not_4_out, D);
  and and_1 (and_1_out, B, D);
  and and_2 (and_2_out, not_2_out, not_4_out);
  and and_3 (and_3_out, not_3_out, not_4_out);
  and and_4 (and_4_out, D, C);
  and and_5 (and_5_out, not_2_out, not_4_out);
  and and_6 (and_6_out, not_2_out, C);
  and and_7 (and_7_out, B, not_3_out, D);
  and and_8 (and_8_out, C, not_4_out);
  and and_9 (and_9_out, not_2_out, not_4_out);
  and and_10 (and_10_out, C, not_4_out);
  and and_11 (and_11_out, not_3_out, not_4_out);
  and and_12 (and_12_out, B, not_3_out);
  and and_13 (and_13_out, B, not_4_out);
  and and_14 (and_14_out, not_2_out, C);
  and and_15 (and_15_out, B, not_3_out);
  and and_16 (and_16_out, B, not_4_out);
  and and_17 (and_17_out, A, B, C);
  and and_18 (and_18_out, A, B);
  and and_19 (and_19_out, A, C);
  or or_1 (or_1_out, and_1_out, and_2_out, C, A);
  or or_2 (or_2_out, and_3_out, not_2_out, and_4_out);
  or or_3 (or_3_out, not_3_out, D, B);
  or or_4 (or_4_out, and_5_out, and_6_out, and_7_out, A, and_8_out);
  or or_5 (or_5_out, and_9_out, and_10_out);
  or or_6 (or_6_out, and_11_out, and_12_out, and_13_out, A);
  or or_7 (or_7_out, and_14_out, and_15_out, and_16_out, A);
  or or_8 (or_8_out, and_17_out, and_18_out, and_19_out);
  nand nand_1 (nand_1_out, or_1_out, or_8_out);
  nand nand_2 (nand_2_out, or_2_out, or_8_out);
  nand nand_3 (nand_3_out, or_3_out, or_8_out);
  nand nand_4 (nand_4_out, or_8_out, or_4_out);
  nand nand_5 (nand_5_out, or_5_out, or_8_out);
  nand nand_6 (nand_6_out, or_6_out, or_8_out);
  nand nand_7 (nand_7_out, or_8_out, or_7_out);
  and and_20 (a_2, nand_1_out, or_1_out);
  and and_21 (b_2, nand_2_out, or_2_out);
  and and_22 (c_2, nand_3_out, or_3_out);
  and and_23 (d_2, nand_4_out, or_4_out);
  and and_24 (e, nand_5_out, or_5_out);
  and and_25 (f, nand_6_out, or_6_out);
  and and_26 (g, nand_7_out, or_7_out);
  _7_Segment_Display u_7_segment_display_1 (.g(g), .f(f), .a(a_2), .b(b_2), .e(e), .d(d_2), .c(c_2));  // open: dp
endmodule

module p2 (
  input  in_1
);

  wire clock_1_out, j_k_ff_1_q, j_k_ff_1_qn, j_k_ff_2_q, j_k_ff_2_qn, j_k_ff_3_q, j_k_ff_3_qn, j_k_ff_4_q,
       main_1_a_2, main_1_b_2, main_1_c_2, main_1_d_2, main_1_e, main_1_f, main_1_g;

  Clock clock_1 (.out(clock_1_out));
  J_K_Flip_Flop j_k_ff_1 (
    .J(in_1), .clk(clock_1_out), .K(in_1), .Q(j_k_ff_1_q), .Qn(j_k_ff_1_qn), .en(in_1));  // open: preset, reset
  J_K_Flip_Flop j_k_ff_2 (
    .J(in_1), .clk(j_k_ff_1_qn), .K(in_1), .Q(j_k_ff_2_q), .Qn(j_k_ff_2_qn), .en(in_1));  // open: preset, reset
  J_K_Flip_Flop j_k_ff_3 (
    .J(in_1), .clk(j_k_ff_2_qn), .K(in_1), .Q(j_k_ff_3_q), .Qn(j_k_ff_3_qn), .en(in_1));  // open: preset, reset
  J_K_Flip_Flop j_k_ff_4 (.J(in_1), .clk(j_k_ff_3_qn), .K(in_1), .Q(j_k_ff_4_q), .en(in_1));  // open: Qn, preset, reset
  main main_1 (
    .A(j_k_ff_4_q), .B(j_k_ff_3_q), .C(j_k_ff_2_q), .D(j_k_ff_1_q), .a_2(main_1_a_2), .b_2(main_1_b_2),
    .c_2(main_1_c_2), .d_2(main_1_d_2), .e(main_1_e), .f(main_1_f), .g(main_1_g));
  _7_Segment_Display u_7_segment_display_1 (
    .g(main_1_g), .f(main_1_f), .a(main_1_a_2), .b(main_1_b_2), .e(main_1_e), .d(main_1_d_2), .c(main_1_c_2));  // open: dp
endmodule
